# Fritzing sketch i2c_fm_transmitter (saved by Fritzing 0.9.4)
breadboards: 1

parts:
  Part1 = Si4713 Stereo FM Transmitter
  BATT1 = 4xAA Switchable Battery Pack w/Bare Wire
  U1 = LuaNode32 / ESP32 [part_number=ESP32S-PIN30]
  Part5 = Adafruit MPM3610
  LED1 = LED - 3mm [color="Red (633nm)" package="3 mm [THT]"]
  R1 = Resistor [tolerance=±5% resistance=220 package="0805 [SMD]"]
  ANT1 = Antenna

nets:
  N1: Part1.ANT, ANT1.antenna_lead
  VIN: Part1.VIN, Part1.CS, U1.EN, U1.3V3, Part5.3.3V
  GND: Part1.GND, BATT1.NEG, U1.GND, Part5.GND, LED1.anode
  N2: Part1.SDA, U1.D21
  N3: Part1.SCL, U1.D22
  N4: Part1.RST, U1.D5, R1.Pin_1
  N5: BATT1.POS, Part5.EN, Part5.VIN
  N6: LED1.cathode, R1.Pin_0

notes:
  Orange -- Vin (5v-to-21v)
  Red -- 3v3
  Yellow -- (I2C) SCL
  Green -- (I2C) SDA
  Blue -- Reset/Enable Signals (All Active Low)
  MPM3610
  Buck 5v-to-21v input to 3v3. This allows 12v Cigarrete Port Charger as power supply (for use in my car)
  SI4713
  Aux-to-FM transmitter. FM frequency controlled by I2C bus.
  I2C Addr: (CS HIGH) 0x63
  (CS LOW) 0x11
  ESP32-WROOM-32
  I2C Master. BLE and WIFI capabilities... might be possible to use these as audio inputs in the future.
  Left (Pink) Right (Cyan) analog inputs (~0.7v) for FM transmitter. Not currently used, but could be useful for future BLE/WIFI audio input

custom parts:
  Si4713 Stereo FM Transmitter: Yaaar! Become your very own pirate radio station with this FM radio transmitter. This breakout board, based on the best-of-class Si4713, is an all-in-one stereo audio FM transmitter that can also transmit RDS/RBDS data!
  4xAA Switchable Battery Pack w/Bare Wire: 4xAA Switchable Battery Pack with Bare Wire connection
  LuaNode32 / ESP32: New Image for LuaNode32 DOIT ESP32 DEVKIT V1. Base parts from LuaNode32 / ESP32 ESP32 based LuaNode32 by G.Noorlander DOIT Esp32 DevKit v1 (30 pins long, 11 pins width) by Werner Rothschopf (modified by vanepp Dec 2018)
